# Fritzing sketch 1.2 (saved by Fritzing 0.9.3b)
breadboards: 1

parts:
  BASE1 = BASE32 [package=THT]
  LED1 = LED - 5mm [color="Red (633nm)" package="5 mm [THT]"]
  R1 = Resistor [tolerance=±5% resistance=220 package=THT]
  LED2 = LED - 5mm [color="Green (565nm)" package="5 mm [THT]"]
  R2 = Resistor [tolerance=±5% resistance=220 package=THT]

nets:
  N1: BASE1.GND, R1.Pin_1, R2.Pin_1
  N2: BASE1.IO17, LED1.anode
  N3: BASE1.IO16, LED2.anode
  N4: LED1.cathode, R1.Pin_0
  N5: LED2.cathode, R2.Pin_0

custom parts:
  BASE32: ESP32 extension board
