# Fritzing sketch 3.4 (saved by Fritzing 0.9.3b)
breadboards: 1

parts:
  BASE1 = BASE32 [package=THT]
  Mod1 = KY-019 5V Relay Module [package="Breakout board"]
  R1 = Resistor [tolerance=±5% resistance=220 package=THT]
  LED1 = LED - 5mm [color="Red (633nm)" package="5 mm [THT]"]

nets:
  N1: BASE1.VCC#45, LED1.cathode
  N2: BASE1.VCC#48, Mod1.Common
  N3: BASE1.GND, Mod1.-
  N4: BASE1.IO15, Mod1.S
  N5: BASE1.5V, Mod1.+
  N6: Mod1.NO, R1.Pin_1
  N7: R1.Pin_0, LED1.anode

custom parts:
  BASE32: ESP32 extension board
  KY-019 5V Relay Module: KY-019 5V Relay module, used to control AC circuits. (Special thanks to vanepp for fixing the PCB holes and other errors)
