# Fritzing sketch 4.2 (saved by Fritzing 0.9.3b)
breadboards: 1

parts:
  BASE1 = BASE32 [package=THT]
  S1 = Pushbutton [package="[THT]"]
  R1 = Resistor [tolerance=±5% resistance=10k package=THT]
  LED1 = LED - 5mm [color="Red (633nm)" package="5 mm [THT]"]
  R2 = Resistor [tolerance=±5% resistance=220 package=THT]

nets:
  N1: BASE1.VCC, S1.Pin_3, S1.Pin_4
  N2: BASE1.GND, R1.Pin_1, R2.Pin_1
  N3: BASE1.IO16, LED1.anode
  N4: BASE1.IO2, S1.Pin_1, S1.Pin_2, R1.Pin_0
  N5: LED1.cathode, R2.Pin_0

custom parts:
  BASE32: ESP32 extension board
