# Fritzing sketch 5.1 (saved by Fritzing 0.9.3b)
breadboards: 1

parts:
  BASE1 = BASE32 [package=THT]
  R1 = Rotary Potentiometer (Small) [maximum_resistance=100kΩ package=THT]

nets:
  N1: BASE1.GND, R1.leg1
  N2: BASE1.VCC, R1.leg2
  N3: BASE1.IO35, R1.wiper

custom parts:
  BASE32: ESP32 extension board
