# Fritzing sketch 5.2 (saved by Fritzing 0.9.3b)
breadboards: 1

parts:
  BASE1 = BASE32 [package=THT]
  R1 = Photocell (LDR) [package=THT]
  R2 = Resistor [tolerance=±5% resistance=10k package=THT]

nets:
  N1: BASE1.GND, R2.Pin_1
  N2: BASE1.VCC, R1.pin_1
  N3: BASE1.IO35, R1.pin_0, R2.Pin_0

custom parts:
  BASE32: ESP32 extension board
