# Fritzing sketch 5.4 (saved by Fritzing 0.9.3b)

parts:
  BASE1 = BASE32 [package=THT]
  Part1 = FC-28 Soil Hygrometer Module - Probe
  Part2 = FC-28 Soil Hygrometer Module

nets:
  GND: BASE1.GND, Part2.GND
  VCC: BASE1.VCC, Part2.VCC
  N1: BASE1.IO35, Part2.AO
  N2: Part1.POS, Part2.POS
  N3: Part1.NEG, Part2.NEG

custom parts:
  BASE32: ESP32 extension board
  FC-28 Soil Hygrometer Module - Probe: The FC-28 is a soil hygrometer module that uses the Texas Instruments LM393 comparator chip to provide an analog measurement of soil humidity.
  FC-28 Soil Hygrometer Module: The FC-28 is a soil hygrometer module that uses the Texas Instruments LM393 comparator chip to provide an analog measurement of soil humidity. The digital output is high when soil moisture is over a certain threshold, as determined by adjusting the potentiometer.
