# Fritzing sketch 5.5 (saved by Fritzing 0.9.3b)
breadboards: 1

parts:
  BASE1 = BASE32 [package=THT]
  U1 = TMP36 [package=to-92]

nets:
  GND: BASE1.GND, U1.GND
  VCC: BASE1.VCC, U1.VCC
  N1: BASE1.IO35, U1.VOUT

custom parts:
  BASE32: ESP32 extension board
