# Fritzing sketch 6.1 (saved by Fritzing 0.9.3b)
breadboards: 1

parts:
  BASE1 = BASE32 [package=THT]
  LED1 = LED - 5mm [color="Red (633nm)" package="5 mm [THT]"]
  R2 = Resistor [tolerance=±5% resistance=220 package=THT]

nets:
  N1: BASE1.GND, LED1.cathode
  N2: BASE1.IO12, R2.Pin_1
  N3: LED1.anode, R2.Pin_0

custom parts:
  BASE32: ESP32 extension board
