# Fritzing sketch 6.2 (saved by Fritzing 0.9.3b)
breadboards: 1

parts:
  BASE1 = BASE32 [package=THT]
  R1 = Rotary Potentiometer (Small) [maximum_resistance=100kΩ package=THT]
  LED1 = LED - 5mm [color="Red (633nm)" package="5 mm [THT]"]
  R2 = Resistor [tolerance=±5% resistance=220 package=THT]

nets:
  N1: BASE1.GND, R1.leg1, LED1.cathode
  N2: BASE1.VCC, R1.leg2
  N3: BASE1.IO35, R1.wiper
  N4: BASE1.IO12, R2.Pin_1
  N5: LED1.anode, R2.Pin_0

custom parts:
  BASE32: ESP32 extension board
