# Fritzing sketch 7.1 (saved by Fritzing 0.9.3b)

parts:
  BASE1 = BASE32 [package=THT]
  J1 = Basic Servo

nets:
  GND: BASE1.GND, J1.gnd
  N1: BASE1.IO25, J1.pulse
  5V: BASE1.5V, J1.vcc

custom parts:
  BASE32: ESP32 extension board
