# Fritzing sketch 7.2 (saved by Fritzing 0.9.3b)
breadboards: 1

parts:
  BASE1 = BASE32 [package=THT]
  J1 = Basic Servo
  RE1 = Rotary Encoder [package=THT]

nets:
  N1: BASE1.GND#9, RE1.EncoderPinA
  N2: BASE1.GND#22, J1.gnd
  N3: BASE1.VCC, RE1.EncoderPinB
  N4: BASE1.IO34, RE1.EncoderPinC
  N5: BASE1.IO25, J1.pulse
  5V: BASE1.5V, J1.vcc

custom parts:
  BASE32: ESP32 extension board
