# Fritzing sketch 8.1 (saved by Fritzing 0.9.3b)

parts:
  BASE1 = BASE32 [package=THT]
  Part1 = SRF05 Ultrasonic Rangefinder

nets:
  GND: BASE1.GND, Part1.GND
  VCC: BASE1.VCC, Part1.VCC
  N1: BASE1.IO14, Part1.Echo
  N2: BASE1.IO12, Part1.Trig

custom parts:
  BASE32: ESP32 extension board
