# Fritzing sketch 9.2 (saved by Fritzing 0.9.3b)
breadboards: 1

parts:
  BASE1 = BASE32 [package=THT]
  LED1 = LED - 5mm [color="Green (555nm)" package="5 mm [THT]"]
  LED2 = LED - 5mm [color="Yellow (585nm)" package="5 mm [THT]"]
  LED3 = LED - 5mm [color="Red (633nm)" package="5 mm [THT]"]
  R1 = Resistor [tolerance=±5% resistance=220 package=THT]
  R2 = Resistor [tolerance=±5% resistance=220 package=THT]
  R3 = Resistor [tolerance=±5% resistance=220 package=THT]

nets:
  N1: BASE1.GND#72, R1.Pin_1, R3.Pin_1
  N2: BASE1.IO17, LED3.anode
  N3: BASE1.IO16, LED2.anode
  N4: BASE1.IO4, LED1.anode
  N5: LED1.cathode, R3.Pin_0
  N6: LED2.cathode, R2.Pin_0
  N7: LED3.cathode, R1.Pin_0

custom parts:
  BASE32: ESP32 extension board
